# Fritzing sketch WakeOnTime (saved by Fritzing 0.9.3b)
breadboards: 1

parts:
  Part1 = Arduino Nano (Rev3.0) [part_number="Arduino Nano 33 IoT"]
  RTC_Clock_DS3231 = Real Time Clock Module - DS1307 RTC Breakout Board [part_number="Chronodot 2.1"]
  Q1 = NPN-Transistor [part_number=BC547B package="SOT-23 [SMD]"]
  R2 = Resistor [tolerance=±5% resistance=100k package=THT]
  Q2 = Basic FET N-Channel [part_number=STP16NF06 package="TO220 [THT]"]
  R3 = Resistor [tolerance=±5% resistance=100k package=THT]
  VCC = 4 x AAA Battery Mount [part_number=5V]
  C1 = Electrolytic Capacitor [capacitance=0.1mF voltage=20V package="100 mil [THT, electrolytic]"]
  C2 = Electrolytic Capacitor [capacitance=0.1mF voltage=20V package="100 mil [THT, electrolytic]"]

nets:
  N1: Part1.GND, Q2.drain, C2.-
  VIN: Part1.VIN, RTC_Clock_DS3231.5V, R2.Pin_1, R3.Pin_0, VCC.+, C1.+, C2.+
  N2: Part1.A5, RTC_Clock_DS3231.SCL
  N3: Part1.A4, RTC_Clock_DS3231.SDA
  N4: RTC_Clock_DS3231.GND, Q1.2, Q2.source, VCC.-, C1.-
  N5: RTC_Clock_DS3231.SQW, Q1.0, R2.Pin_0
  N6: Q1.1, Q2.gate, R3.Pin_1
